// Logisim project arc.circ as structural Verilog: 7 circuits, main circuit main
module main (
  input  A,
  input  C,
  input  B,
  output VAI_1,
  output S
);

  wire and_1_out, and_2_out, or_1_out, xor_2_out;

  xor xor_1 (S, A, xor_2_out);
  xor xor_2 (xor_2_out, B, C);
  and and_1 (and_1_out, B, C);
  or or_1 (or_1_out, C, B);
  and and_2 (and_2_out, or_1_out, A);
  or or_2 (VAI_1, and_2_out, and_1_out);
endmodule

module add_1 (
  input  in_1,
  input  in_2,
  input  in_3
);

  main main_1 (.A(in_1), .C(in_3), .B(in_2));  // open: VAI_1, S
endmodule

// 4
module add_4 (
  input  [3:0] in_1,
  input  [3:0] in_2,
  input  in_3,
  output [3:0] out_4
);

  wire main_1_vai_1, main_2_vai_1, main_3_vai_1, main_4_vai_1;

  // Probe on in_2
  main main_1 (.A(in_1[0]), .C(in_3), .VAI_1(main_1_vai_1), .S(out_4[0]), .B(in_2[0]));
  // Probe on out_4
  main main_2 (.A(in_1[1]), .C(main_1_vai_1), .VAI_1(main_2_vai_1), .S(out_4[1]), .B(in_2[1]));
  // Probe on in_1
  main main_3 (.A(in_1[2]), .C(main_2_vai_1), .VAI_1(main_3_vai_1), .S(out_4[2]), .B(in_2[2]));
  main main_4 (.A(in_1[3]), .C(main_3_vai_1), .VAI_1(main_4_vai_1), .S(out_4[3]), .B(in_2[3]));
  // also tied to GND on the sheet: main_4_vai_1
endmodule

module sub_1 (
  input  A,
  input  C,
  input  B,
  output VAI_1,
  output S
);

  wire and_1_out, and_2_out, or_1_out, xor_2_out;

  xor xor_1 (S, A, xor_2_out);
  xor xor_2 (xor_2_out, B, C);
  and and_1 (and_1_out, B, C);
  or or_1 (or_1_out, C, B);
  and and_2 (and_2_out, or_1_out, ~A);  // AND_Gate
  or or_2 (VAI_1, and_2_out, and_1_out);
endmodule

module sub_4 (
  input  [3:0] in_1,
  input  [3:0] in_2,
  input  in_3,
  output [3:0] out_4
);

  wire sub_1_1_vai_1, sub_1_2_vai_1, sub_1_3_vai_1, sub_1_4_vai_1;

  // Probe on in_2
  sub_1 sub_1_1 (.A(in_1[0]), .C(in_3), .B(in_2[0]), .VAI_1(sub_1_1_vai_1), .S(out_4[0]));
  // Probe on out_4
  sub_1 sub_1_2 (.A(in_1[1]), .C(sub_1_1_vai_1), .B(in_2[1]), .VAI_1(sub_1_2_vai_1), .S(out_4[1]));
  // Probe on in_1
  sub_1 sub_1_3 (.A(in_1[2]), .C(sub_1_2_vai_1), .B(in_2[2]), .VAI_1(sub_1_3_vai_1), .S(out_4[2]));
  sub_1 sub_1_4 (.A(in_1[3]), .C(sub_1_3_vai_1), .B(in_2[3]), .VAI_1(sub_1_4_vai_1), .S(out_4[3]));
  // also tied to GND on the sheet: sub_1_4_vai_1
endmodule

module rot_esq (
  input  [3:0] in_1,
  input  [1:0] in_2,
  output [3:0] out_3
);

  wire and_1_out, and_2_out, and_3_out, and_4_out, and_5_out, and_6_out, and_7_out, and_8_out, and_9_out;

  and and_1 (and_1_out, in_1[3], ~in_2[1], ~in_2[0]);  // AND_Gate
  and and_2 (and_2_out, in_1[2], ~in_2[1], in_2[0]);  // AND_Gate
  and and_3 (and_3_out, in_1[1], in_2[1], ~in_2[0]);  // AND_Gate
  and and_4 (and_4_out, in_1[0], in_2[1], in_2[0]);
  and and_5 (and_5_out, in_1[2], ~in_2[1], ~in_2[0]);  // AND_Gate
  and and_6 (and_6_out, in_1[1], ~in_2[1], in_2[0]);  // AND_Gate
  and and_7 (and_7_out, in_1[0], in_2[1], ~in_2[0]);  // AND_Gate
  and and_8 (and_8_out, in_1[1], ~in_2[1], ~in_2[0]);  // AND_Gate
  and and_9 (and_9_out, in_1[0], ~in_2[1], in_2[0]);  // AND_Gate
  and and_10 (out_3[0], in_1[0], ~in_2[1], ~in_2[0]);  // AND_Gate
  or or_1 (out_3[2], and_5_out, and_6_out, and_7_out);
  or or_2 (out_3[3], and_1_out, and_2_out, and_3_out, and_4_out);
  or or_3 (out_3[1], and_8_out, and_9_out);

  // Notes on the sheet:
  //   and_10 drives only 0 and floats otherwise
endmodule

module rot_diret (
  input  [3:0] in_1,
  input  [1:0] in_2,
  output [3:0] out_3
);

  wire and_1_out, and_2_out, and_3_out, and_4_out, and_5_out, and_6_out, and_7_out, and_8_out, and_9_out;

  and and_1 (and_1_out, in_1[0], ~in_2[1], ~in_2[0]);  // AND_Gate
  and and_2 (and_2_out, in_1[1], ~in_2[1], in_2[0]);  // AND_Gate
  and and_3 (and_3_out, in_1[2], in_2[1], ~in_2[0]);  // AND_Gate
  and and_4 (and_4_out, in_1[3], in_2[1], in_2[0]);
  and and_5 (and_5_out, in_1[1], ~in_2[1], ~in_2[0]);  // AND_Gate
  and and_6 (and_6_out, in_1[2], ~in_2[1], in_2[0]);  // AND_Gate
  and and_7 (and_7_out, in_1[3], in_2[1], ~in_2[0]);  // AND_Gate
  and and_8 (and_8_out, in_1[2], ~in_2[1], ~in_2[0]);  // AND_Gate
  and and_9 (and_9_out, in_1[3], ~in_2[1], in_2[0]);  // AND_Gate
  and and_10 (out_3[3], in_1[3], ~in_2[1], ~in_2[0]);  // AND_Gate
  or or_1 (out_3[1], and_5_out, and_6_out, and_7_out);
  or or_2 (out_3[0], and_1_out, and_2_out, and_3_out, and_4_out);
  or or_3 (out_3[2], and_8_out, and_9_out);

  // Notes on the sheet:
  //   and_10 drives only 0 and floats otherwise
endmodule
