// Logisim project somador 4 bit.circ as structural Verilog: 3 circuits, main circuit main
module main (
  input  A,
  input  C,
  input  B,
  output VAI_1,
  output S
);

  wire and_1_out, and_2_out, or_1_out, xor_2_out;

  xor xor_1 (S, A, xor_2_out);
  xor xor_2 (xor_2_out, B, C);
  and and_1 (and_1_out, B, C);
  or or_1 (or_1_out, C, B);
  and and_2 (and_2_out, or_1_out, A);
  or or_2 (VAI_1, and_2_out, and_1_out);
endmodule

module add (
  input  in_1,
  input  in_2,
  input  in_3,
  input  in_4,
  input  in_5,
  input  in_6,
  output out_7,
  output out_8
);

  main main_1 (.A(in_1), .C(in_3), .B(in_2));  // open: VAI_1, S
  main main_2 (.A(in_5), .C(in_6), .VAI_1(out_7), .S(out_8), .B(in_6));
endmodule

// 4
module add_4 (
  input  [3:0] in_1,
  input  [3:0] in_2,
  input  in_3,
  output [3:0] out_4
);

  wire main_1_vai_1, main_2_vai_1, main_3_vai_1, main_4_vai_1;

  // Probe on in_2
  main main_1 (.A(in_1[0]), .C(in_3), .VAI_1(main_1_vai_1), .S(out_4[0]), .B(in_2[0]));
  // Probe on out_4
  main main_2 (.A(in_1[1]), .C(main_1_vai_1), .VAI_1(main_2_vai_1), .S(out_4[1]), .B(in_2[1]));
  // Probe on in_1
  main main_3 (.A(in_1[2]), .C(main_2_vai_1), .VAI_1(main_3_vai_1), .S(out_4[2]), .B(in_2[2]));
  main main_4 (.A(in_1[3]), .C(main_3_vai_1), .VAI_1(main_4_vai_1), .S(out_4[3]), .B(in_2[3]));
  // also tied to GND on the sheet: main_4_vai_1
endmodule
